# Fritzing sketch blink_led (saved by Fritzing 0.9.3b)
breadboards: 1

parts:
  부품1 = Arduino Uno (Rev3)
  LED1 = LED - 5mm [color="Red (633nm)" package="5 mm [THT]"]
  LED2 = LED - 5mm [color="Green (555nm)" package="5 mm [THT]"]
  R1 = Resistor [tolerance=±5% resistance=220 package=THT]  # not connected
  R2 = Resistor [tolerance=±5% resistance=220 package=THT]

nets:
  N1: 부품1.D8, LED2.anode
  N2: 부품1.D10_PWM/SS, LED1.anode
  N3: 부품1.GND, R2.Pin_1
  N4: LED2.cathode, R2.Pin_0
